# Fritzing sketch Servo Controller (saved by Fritzing 0.9.3b)
breadboards: 1

parts:
  R1 = Resistor [tolerance=±5% resistance=56k package=THT]
  R2 = Resistor [tolerance=±5% resistance=3M package=THT]
  D1 = Rectifier Diode [part_number=1N4148 package="300 mil [THT]"]
  C1 = Ceramic Capacitor [capacitance=100nF package="100 mil [THT, multilayer]"]
  Power_plug1 = Power plug
  J1 = Basic Servo
  U1 = 555 Timer [package="DIP8 [THT]"]
  R3 = Rotary Potentiometer (Small) [maximum_resistance=100kΩ package=THT]

nets (from the schematic view):
  N1: R1.Pin_0, R3.leg2
  VCC: R1.Pin_1, Power_plug1.VCC, J1.vcc, U1.Reset, U1.Vcc_Supply_Voltage
  N2: R2.Pin_0, D1.cathode, C1.1, U1.Trigger
  N3: R2.Pin_1, D1.anode, U1.Discharge, R3.leg1, R3.wiper
  GND: C1.0, Power_plug1.GND, J1.gnd, U1.Ground
  N4: J1.pulse, U1.Output
